# Fritzing sketch transmitter (saved by Fritzing 0.8.5b)
breadboards: 1

parts:
  Part1 = Arduino Uno (Rev3)  # not connected
  Part2 = Arduino Leonardo (Rev3b)
  R1 = Resistor [tolerance=±5% resistance=10 package=THT]
  C1 = Ceramic Capacitor [capacitance=4.7µF voltage=6.3V package="100 mil [THT, multilayer]"]
  Q1 = NPN-Transistor [package="TO92 [THT]"]
  LED1 = LED - 5mm [color="Red (633nm)" package="5 mm [THT]"]  # not connected

nets (from the breadboard view):
  N1: Part2.D4/A6, Q1.B
  N2: Part2.5V, R1.Pin_0, C1.1
  N3: Part2.GND, C1.0, Q1.C
  N4: R1.Pin_1, Q1.E
